# Fritzing sketch N1 pcb layout rev0 (saved by Fritzing 0.9.3b)
circuit board: 6.5cm x 5.64cm
breadboards: 1

parts:
  r-101 = Resistor [tolerance=±5% resistance=10k package=THT]
  r-102 = Resistor [tolerance=±5% resistance=10k package=THT]
  s-101 = Pushbutton [package="[THT]"]
  s-102 = Pushbutton [package="[THT]"]
  r-103 = Resistor [tolerance=±5% resistance=220 package=THT]
  r-104 = Resistor [tolerance=±5% resistance=220 package=THT]
  r-105 = Resistor [tolerance=±5% resistance=220 package=THT]
  lt-101 = LED - 5mm [color="Red (633nm)" package="5 mm [THT]"]
  lt-102 = LED - 5mm [color="Yellow (595nm)" package="5 mm [THT]"]
  lt-103 = LED - 5mm [color="Green (570nm)" package="5 mm [THT]"]
  dig-11 = rounded female pin header, 1 pin [form="♀ (female rounded)"]
  dig-10 = rounded female pin header, 1 pin [form="♀ (female rounded)"]
  gnd = female pin header, 8 pins [form="♀ (female)"]
  vcc = female pin header, 8 pins [form="♀ (female)"]
  dig-7 = rounded female pin header, 1 pin [form="♀ (female rounded)"]
  dig-4 = rounded female pin header, 1 pin [form="♀ (female rounded)"]
  dig-2 = rounded female pin header, 1 pin [form="♀ (female rounded)"]

nets:
  N1: r-101.Pin_0, r-102.Pin_0, r-103.Pin_1, r-104.Pin_1, r-105.Pin_1, gnd.pin1, gnd.pin2, gnd.pin3, gnd.pin4, gnd.pin5, gnd.pin6, gnd.pin7, gnd.pin8
  N2: r-101.Pin_1, s-101.Pin_3, s-101.Pin_4, dig-11.pin1
  N3: r-102.Pin_1, s-102.Pin_3, s-102.Pin_4, dig-10.pin1
  N4: s-101.Pin_1, s-101.Pin_2, s-102.Pin_1, s-102.Pin_2, vcc.pin1, vcc.pin2, vcc.pin3, vcc.pin4, vcc.pin5, vcc.pin6, vcc.pin7, vcc.pin8
  N5: r-103.Pin_0, lt-101.anode
  N6: r-104.Pin_0, lt-102.anode
  N7: r-105.Pin_0, lt-103.anode
  N8: lt-101.cathode, dig-7.pin1
  N9: lt-102.cathode, dig-4.pin1
  N10: lt-103.cathode, dig-2.pin1
